# Fritzing sketch SousVideLogger (saved by Fritzing 0.9.3b)
breadboards: 2

parts:
  WeMos_D1_Mini1 = WeMos D1 Mini
  LCD1 = LCD screen
  DS2 = DS18B20 1-Wire Temperature Sensor [part_number=DS18B20]
  DS3 = DS18B20 1-Wire Temperature Sensor [part_number=DS18B20]
  DS4 = DS18B20 1-Wire Temperature Sensor [part_number=DS18B20]
  DS5 = DS18B20 1-Wire Temperature Sensor [part_number=DS18B20]
  R1 = Resistor [tolerance=±5% resistance=68 package=THT]
  R2 = Resistor [tolerance=±5% resistance=1.8k package=THT]
  R3 = Resistor [tolerance=±5% resistance=4.7k package=THT]

nets:
  VDD: WeMos_D1_Mini1.5V, DS2.VDD, DS3.VDD, DS4.VDD, DS5.VDD, R3.Pin_1
  GND: LCD1.VSS, LCD1.LED-, DS2.GND, DS3.GND, DS4.GND, DS5.GND, R2.Pin_1
  N1: LCD1.VDD, R1.Pin_0
  N2: LCD1.V0, R2.Pin_0
  N3: LCD1.LED+, R1.Pin_1
  N4: DS2.DQ, DS3.DQ, DS4.DQ, DS5.DQ, R3.Pin_0
